# Fritzing sketch CollarDesign (saved by Fritzing 0.9.6b)
circuit board: 7.62cm x 6.69505cm
breadboards: 2

parts:
  Part1 = Mono 2.5W Class D Audio Amplifier - PAM8302
  VCC1 = Battery block 9V
  LED1 = LED - 3mm [color="Green (555nm)" current=0.030 package="3 mm [THT]"]
  Part2 = OLED Monochrome 128x64 1.3 inch [part_number=938]
  S1 = Toggle Switch [package=THT]
  R2 = Resistor [tolerance=±1% resistance=220 power=0.25 package=THT]
  R1 = Resistor [tolerance=±1% resistance=150 power=0.25 package=THT]
  R3 = Resistor [tolerance=±1% resistance=220 power=0.25 package=THT]
  U2 = atmega328 [package=dip]
  U1 = ESP32S-HiLetgo [part_number=ESP32S-HiLetgo]
  U3 = SUP500F [package=sup500f]

nets:
  GND: Part1.GND, VCC1.-, LED1.cathode, Part2.GND, R2.Pin_1, R3.Pin_1, U2.GND#7, U1.GND, U3.GND
  VCC: Part1.VCC, Part2.VIN, S1.COM, U2.VCC, U2.A0, U1.VIN, U3.VCC
  N1: Part1.AIN+, U1.GPIO25
  N2: VCC1.+, R1.Pin_0
  N3: LED1.anode, U2.D6_(PWM)
  N4: Part2.MOSI_SDA, U2.A4
  N5: Part2.SCLK_SCK, U2.A5
  N6: S1.L1, R2.Pin_0, R1.Pin_1
  N7: R3.Pin_0, U2.D1_(TX), U1.GPIO16
  N8: U2.D0_(RX), U1.GPIO17
  N9: U2.XLAT2, U3.RX-I
  N10: U2.D5_(PWM), U3.TX-O

notes:
  5V

custom parts:
  Mono 2.5W Class D Audio Amplifier - PAM8302: A super small but powerful mono amplifier able to deliver up to 2.5 Watts into 4-8 ohm impedance speakers. Inside the miniature chip is a class D controller, able to run from 2.0V-5.5VDC. Since the amp is a class D, its very efficient (over 90% efficient when driving an 8Ω speaker at over half a Watt) - making it perfect for portable and battery-powered projects.
  OLED Monochrome 128x64 1.3 inch: These displays are small, only about 1.3" diagonal, but very readable due to the high contrast of an OLED display. This display is made of 128x64 individual white OLED pixels, each one is turned on or off by the controller chip. Because the display makes its own light, no backlight is required. This reduces the power required to run the OLED and is why the display has such high contrast; we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
  ESP32S-HiLetgo: HiLetgo ESP-WROOM-32 ESP32 ESP-32S Development Board 2.4GHz Dual-Mode WiFi + Bluetooth Dual Cores Microcontroller The ESP32 integrated with Antenna switches, RF Balun, power amplifiers, low-noise amplifiers, filters, and management modules, and the entire solution occupies the least area of PCB. 2.4 GHz Wi-Fi plus Bluetooth dual-mode chip, with TSMC Ultra-low power consumption 40nm technology,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
